# Fritzing sketch Untitled Sketch 2 (saved by Fritzing 0.9.3b)
breadboards: 1

parts:
  M1 = MakerFocus MAX30102
  CPU1 = NodeMCU WROOM ESP 32
  OLED_I2C1 = OLED 128x64 I2C Monochrome Display
  SG1 = Buzzer 12mm [part_number=COM-07950 package=buzzer-12mm-ns]

nets:
  GND: M1.GND, CPU1.pin_18, OLED_I2C1.GND, SG1.2
  N1: M1.SCL, OLED_I2C1.SCK
  N2: M1.SDA, OLED_I2C1.SDA
  VIN: M1.VIN, CPU1.pin_17, OLED_I2C1.VDD
  N3: CPU1.pin_8, CPU1.pin_24, CPU1.pin_28
  N4: CPU1.pin_9, CPU1.pin_25
  N5: CPU1.pin_19, SG1.1

custom parts:
  MakerFocus MAX30102: Oximeter module using the MAX30102 chip. As usual, if you want the mounting holes in pcb, you need to drag a hole over the pad in silkscreen to actually drill the hole (by default they are not drilled)
  NodeMCU WROOM ESP 32: 30 pol Development Kit
  Buzzer 12mm: Buzzer 12mm Spark Fun Electronics SKU : Comp-Buzzer Through hole This is a small 12mm round speaker that operates around the audible 2kHz range. You can use these speakers to create simple music or user interfaces. This is not a true piezoelectric speaker but behaves similarly. Instead of a piezoelectric crystal that vibrates with an electric current, this tiny speaker uses an electromagnet to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
